# Fritzing sketch Механизм для форточки  (saved by Fritzing 0.9.10b)

parts:
  J1 = Basic Servo
  J2 = Power Jack [package=power_jack_combo]
  WeMos_D1_Mini1 = WeMos D1 Mini
  C1 = Capacitor [package=cap-pth-small]
  ACS = ACS712 Low Current Sensor Board v12
  S1 = Round Pushbutton

nets:
  GND: J1.gnd, J2.GND, J2.GNDBREAK, WeMos_D1_Mini1.G, C1.1, ACS.GND
  N1: J1.vcc, ACS.IP-
  N2: J1.pulse, WeMos_D1_Mini1.D5
  N3: J2.PWR, S1.leg1
  5V: WeMos_D1_Mini1.5V, C1.2, ACS.5V
  N4: WeMos_D1_Mini1.A0, ACS.VO
  N5: ACS.IP+, S1.leg0

notes:
  Серводвигатель
  DS3230-270
  Открывает и закрывает форточку на заданный угол
  Датчик тока
  ACS712
  Фиксирует ток, протекающий через сервопривод servo. Для определения перегрузки
  Микроконтроллер
  ESP-8266
  Осуществляет управление устройствами
  Реализует подключение к Mesh-сети по Wi-Fi
  Блок питания
  220V - 5V 1.5A
  Блокировочный конденсатор
  0.1 мкф
  Накапливает заряд электрического тока и передает другим электрокомпонентам
  Отсекает обратные токи
  Кнопка питания
  Переключатель SPST
  Ручное управление питанием системы
  Микроконтроллер ESP-8266
  Осуществляет управление устройствами
  Реализует подключение к Mesh-сети по Wi-Fi
  Датчик тока ACS712
  Фиксирует ток, протекающий через сервопривод servo. Для определения перегрузки
  Блокировочный конденсатор
  0.1 мкф
