# Fritzing sketch Система климатических датчиков (saved by Fritzing 0.9.10b)

parts:
  RHT1 = Humidity and Temperature Sensor RHT03
  WeMos_D1_Mini1 = WeMos D1 Mini
  BAT1 = Battery Holders [package=lipo-1100mAh]
  TP1 = TP4056 [chip_label=TP4056 package="DIP (Dual Inline) [THT]"]
  S2 = Round Pushbutton
  Soil = Soil Moisture Sensor

nets:
  VCC: RHT1.Vcc, WeMos_D1_Mini1.5V, S2.leg0, Soil.VCC
  N1: RHT1.Data-signal, WeMos_D1_Mini1.D2
  N2: RHT1.GND_1, RHT1.GND_2, WeMos_D1_Mini1.G, TP1.pin6, Soil.GND
  N3: WeMos_D1_Mini1.A0, Soil.SIG
  N4: BAT1.+, TP1.pin4
  N5: BAT1.-, TP1.pin5
  N6: TP1.pin3, S2.leg1

notes:
  Датчик влажности почвы
  Capacitive Soil Moisture v1.2
  Микроконтроллер
  ESP-8266
  Осуществляет управление устройствами
  Реализует подключение к Mesh-сети по Wi-Fi
  Имеет встроенный преобразователь напряжения
  Кнопка питания
  Переключатель SPST
  Ручное управление питанием системы
  Датчик влажности и температуры воздуха
  DHT11
  Аккумулятор Li-po
  3.7V 800mAh
  Плата защиты и заряда
  TP4056
  Контролирует и защищает аккумулятор от переразряда, перезаряда и смены полярности
  Микроконтроллер ESP-8266
  Осуществляет управление устройствами
  Реализует подключение к Mesh-сети по Wi-Fi

custom parts:
  TP4056: A DIP stand-in part for whatever IC you want. With 6 pins on a 300mil dual inline package (DIP) footprint.
