# Fritzing sketch Система полива и увлажнения (saved by Fritzing 0.9.10b)

parts:
  WeMos_D1_Mini1 = WeMos D1 Mini
  J1 = Power Jack [package=power_jack_slot]
  J2 = Piezo Speaker
  M1 = DC Motor [voltage_(max)=6V voltage_(min)=3V]
  S1 = Round Pushbutton
  Liq = Humidity Sensor - HIH-4030 Breakout
  C1 = Capacitor [package=cap-pth-small-kit]
  Mod1 = KY-019 5V Relay Module [package="Breakout board"]

nets:
  5V: WeMos_D1_Mini1.5V, S1.leg1, Liq.VCC, C1.2, Mod1.+
  N1: WeMos_D1_Mini1.A0, Liq.OUT
  N2: WeMos_D1_Mini1.D2, J2.pin2
  N3: WeMos_D1_Mini1.D5, Mod1.S
  N4: WeMos_D1_Mini1.G, C1.1
  GND: J1.GNDBREAK, J1.GND, J2.pin1, M1.pin_2, Liq.GND, Mod1.-
  N5: J1.PWR, S1.leg0, Mod1.Common
  N6: M1.pin_1, Mod1.NO

notes:
  Микроконтроллер
  ESP-8266
  Реализует подключение к Mesh-сети по Wi-Fi. Осуществляет управление устройствами
  Кнопка питания
  Переключатель SPST
  Ручное управление питанием системы
  Блок питания
  220V - 5V 1.5A
  Реле
  Управляет
  включением/выключением погружного насоса
  Погружной насос
  Механизм полива
  Ультразвуковой увлажнитель воздуха
  Ultrasonic Humidifier
  Поплавковый датчик уровня воды
  P45 Liquid Water Level
  Керамический блокировочный конденсатор
  0.1 мкф
  Накапливает заряд электрического тока и передает другим электрокомпонентам
  Отсекает обратные токи
  Керамический блокировочный конденсатор
  0.1 мкф

custom parts:
  KY-019 5V Relay Module: KY-019 5V Relay module, used to control AC circuits. (Special thanks to vanepp for fixing the PCB holes and other errors)
